# Fritzing sketch Circuito (saved by Fritzing 0.9.3b)
circuit board: 8.46667cm x 5.64444cm
breadboards: 1

parts:
  Componente1 = Arduino Nano (Rev3.0)
  R1 = Resistor [tolerance=±5% resistance=110 package=THT]
  R2 = Rotary Potentiometer (Small) [maximum_resistance=10Ω package=THT]
  LED1 = LED - 5mm [color="Red (633nm)" package="5 mm [THT]"]

nets:
  N1: Componente1.GND, R2.leg1, R2.leg2, LED1.anode
  N2: Componente1.D3, R1.Pin_0
  N3: Componente1.A0, R2.wiper
  N4: R1.Pin_1, LED1.cathode

// code stored in the sketch: Circuito.ino
// C++ code
//
int pwm = 3; // pin del arduino donde se conecta el led
int brillo;
int pot = 0;

void setup()
{
  pinMode(pwm,OUTPUT);
  //analogWrite(pwm,255);
  // Las entradas anal?gicas no requiere inicializaci?n
}

void loop()
{
  /*for (led = 0; led <= 255 ; led++) {
    analogWrite(pwm,led);
    delay(25);
  }
  for (led = 255; led >= 0 ; led--){
    analogWrite(pwm,led);
  }*/
  
  // Control con potenciometro
  
  // El valor de entrada anal?gica es de 0 a 1023
  // Se debe dividir entre 4 (en 1023 hay 4 veces 255)
  brillo = analogRead(pot)/4;
  analogWrite(pwm,brillo);
}
